// Digital circuit CORDICcircuit_draft.dig as structural Verilog
module CORDICcircuit_draft (
  input  [8:0] z_input,
  input  Processing
);

  wire add_1_s, comparator_1_gt, multiplexer_2_out, multiplexer_6_out, not_1_out, sub_1_s;
  wire [8:0] add_3_s, lookuptable_1_out, multiplexer_1_out, multiplexer_4_out, Register_z_q, sub_3_s;
  wire [9:0] add_2_s, multiplexer_3_out, multiplexer_5_out, Register_x_q, Register_y_q, sub_2_s,
       x_shifter_out, y_shifter_out;

  LookUpTable #(.Bits(9)) lookuptable_1 (.out(lookuptable_1_out));  // open: in0, in1, in2, in3, in4, in5, in6, in7, in8, in9
  Multiplexer #(.Bits(9)) multiplexer_1 (
    .sel(not_1_out), .in_0(multiplexer_4_out), .in_1(z_input), .out(multiplexer_1_out));
  Sub sub_1 (.a(Register_y_q[0]), .b(x_shifter_out[0]), .s(sub_1_s));  // open: c_i, c_o
  Add add_1 (.a(Register_y_q[0]), .b(x_shifter_out[0]), .s(add_1_s));  // open: c_i, c_o
  Add #(.Bits(10)) add_2 (.a(Register_x_q), .b(y_shifter_out), .s(add_2_s));  // open: c_i, c_o
  Sub #(.Bits(10)) sub_2 (.a(Register_x_q), .b(y_shifter_out), .s(sub_2_s));  // open: c_i, c_o
  Register #(.Bits(9)) Register_z (.D(multiplexer_1_out), .Q(Register_z_q));  // open: C, en
  Add #(.Bits(9)) add_3 (.a(Register_z_q), .b(lookuptable_1_out), .s(add_3_s));  // open: c_i, c_o
  Sub #(.Bits(9)) sub_3 (.a(Register_z_q), .b(lookuptable_1_out), .s(sub_3_s));  // open: c_i, c_o
  Multiplexer multiplexer_2 (.sel(comparator_1_gt), .in_0(sub_1_s), .in_1(add_1_s), .out(multiplexer_2_out));
  Multiplexer #(.Bits(10)) multiplexer_3 (
    .sel(comparator_1_gt), .in_0(add_2_s), .in_1(sub_2_s), .out(multiplexer_3_out));
  Comparator #(.Bits(9)) comparator_1 (.a(Register_z_q), .b({9{1'b0}}), .gt(comparator_1_gt));  // open: eq, lt
  Multiplexer #(.Bits(9)) multiplexer_4 (
    .sel(comparator_1_gt), .in_0(add_3_s), .in_1(sub_3_s), .out(multiplexer_4_out));
  not not_1 (not_1_out, Processing);
  Multiplexer multiplexer_5 (.sel(not_1_out), .in_0(multiplexer_2_out), .in_1(1'b0), .out(multiplexer_5_out[0]));
  Multiplexer multiplexer_6 (.sel(not_1_out), .in_0(multiplexer_3_out[0]), .in_1(1'b1), .out(multiplexer_6_out));
  Register #(.Bits(10)) Register_y (.D(multiplexer_5_out), .Q(Register_y_q));  // open: C, en
  Register Register_x (.D(multiplexer_6_out), .Q(Register_x_q[0]));  // open: C, en
  BarrelShifter #(.Bits(10), .direction("right")) y_shifter (.in(Register_y_q), .out(y_shifter_out));  // open: shift
  BarrelShifter #(.Bits(10), .barrelSigned("true"), .direction("right")) x_shifter (
    .in(Register_x_q), .out(x_shifter_out));  // open: shift
  // Pins of 1 and 9 bits meet at z_input
  // Pins of 1 and 10 bits meet at multiplexer_3_out
  // Pins of 1 and 10 bits meet at Register_x_q
  // Pins of 1 and 10 bits meet at Register_y_q
  // Pins of 1 and 10 bits meet at x_shifter_out
  // Pins of 1 and 10 bits meet at multiplexer_5_out
  // Pins of 1 and 10 bits meet at 10'h1
  // Pins of 1 and 10 bits meet at {10{1'b0}}
endmodule
